// Logisim project myCPUwire.circ as structural Verilog: 1 circuit, main circuit main
module main (
  input  in_1,
  output [31:0] Instr,
  output [31:0] pc,
  output RegWrite,
  output [4:0] RegAddr,
  output [31:0] RegData,
  output MemWrite,
  output [31:0] MemAddr,
  output [31:0] MemData
);

  wire and_2_out, and_3_out, and_4_out, and_5_out, and_6_out, and_7_out, and_8_out, and_9_out, and_10_out,
       and_11_out, and_12_out, and_13_out, and_14_out, and_15_out, and_16_out, and_17_out, and_18_out,
       and_19_out, and_20_out, clock_1_out, comparator_1_eq, demultiplexer_1_out0, demultiplexer_1_out1,
       demultiplexer_1_out2, demultiplexer_1_out3, demultiplexer_1_out4, demultiplexer_1_out5,
       demultiplexer_1_out6, demultiplexer_1_out7, demultiplexer_1_out8, demultiplexer_1_out9,
       demultiplexer_1_out10, demultiplexer_1_out11, demultiplexer_1_out12, demultiplexer_1_out13,
       demultiplexer_1_out14, demultiplexer_1_out15, demultiplexer_1_out16, demultiplexer_1_out17,
       demultiplexer_1_out18, demultiplexer_1_out19, demultiplexer_1_out20, demultiplexer_1_out21,
       demultiplexer_1_out22, demultiplexer_1_out23, demultiplexer_1_out24, demultiplexer_1_out25,
       demultiplexer_1_out26, demultiplexer_1_out27, demultiplexer_1_out28, demultiplexer_1_out29,
       demultiplexer_1_out30, demultiplexer_1_out31, not_1_out, not_2_out, not_3_out, not_4_out, not_5_out,
       not_6_out, not_7_out, not_8_out, not_9_out, not_10_out, not_11_out, not_12_out, or_1_out, or_3_out,
       or_5_out, or_6_out, or_7_out, or_8_out, or_11_out, priority_encoder_1_gs;
  wire [2:0] and_1_out;
  wire [3:0] priority_encoder_1_out;
  wire [4:0] multiplexer_1_out;
  wire [15:0] bitselector_1_out;
  wire [31:0] _0_q, _1_q, _2_q, _3_q, _4_q, _5_q, _6_q, _7_q, _8_q, _9_q, _10_q, _11_q, _12_q, _13_q, _14_q,
       _15_q, _16_q, _17_q, _18_q, _19_q, _20_q, _21_q, _22_q, _23_q, _24_q, _25_q, _26_q, _27_q, _28_q,
       _29_q, _30_q, _31_q, adder_1_out, adder_2_out, adder_3_out, and_21_out, bit_extender_1_out,
       bit_extender_2_out, bit_extender_3_out, multiplexer_2_out, multiplexer_3_out, multiplexer_6_out,
       multiplexer_7_out, multiplexer_9_out, or_12_out, ram_1_data, register_1_q, shifter_1_out,
       shifter_2_out, shifter_3_out, subtractor_1_out, subtractor_2_out, xor_1_out;

  and and_1 (and_1_out[0], or_7_out, comparator_1_eq);
  assign xor_1_out = 32'h3000 ^ multiplexer_3_out;  // XOR_Gate xor_1, 32 bits wide
  Adder #(.width(32)) adder_1 (.a(pc), .b(32'h4), .out(adder_1_out));  // open: cin, cout
  assign bit_extender_1_out = {{16{Instr[15]}}, Instr[15:0]};  // Bit_Extender bit_extender_1
  Register #(.width(32)) register_1 (.D(xor_1_out), .Q(register_1_q), .clk(clock_1_out), .clr(in_1));  // open: en
  Shifter #(.width(32)) shifter_1 (.in(bit_extender_1_out), .\dist (5'b00010), .out(shifter_1_out));
  assign pc = 32'h3000 ^ register_1_q;  // XOR_Gate xor_2, 32 bits wide
  Adder #(.width(32)) adder_2 (.a(adder_1_out), .b(shifter_1_out), .out(adder_2_out));  // open: cin, cout
  not not_1 (not_1_out, Instr[31]);
  not not_2 (not_2_out, Instr[30]);
  Multiplexer #(.width(5), .enable("false")) multiplexer_1 (
    .in0(Instr[20:16]), .in1(Instr[15:11]), .out(multiplexer_1_out), .sel(or_1_out));
  Multiplexer #(.width(32), .enable("false")) multiplexer_2 (
    .in0(MemAddr), .in1(ram_1_data), .out(multiplexer_2_out), .sel(or_5_out));
  not not_3 (not_3_out, Instr[29]);
  not not_4 (not_4_out, Instr[28]);
  Multiplexer #(.select(3), .width(32), .enable("false")) multiplexer_3 (
    .in0(adder_1_out), .in1(adder_2_out), .in2({pc[31:28], Instr[25:0], 2'b00}),
    .in3({pc[31:28], Instr[25:0], 2'b00}), .in4(and_21_out), .in5(and_21_out), .in6(and_21_out),
    .in7(and_21_out), .out(multiplexer_3_out), .sel(and_1_out));
  Multiplexer #(.width(5), .enable("false")) multiplexer_4 (
    .in0(multiplexer_1_out), .in1({5{1'b1}}), .out(RegAddr), .sel(and_1_out[1]));
  Multiplexer #(.width(32), .enable("false")) multiplexer_5 (
    .in0(multiplexer_2_out), .in1(adder_1_out), .out(RegData), .sel(and_1_out[1]));
  not not_5 (not_5_out, Instr[27]);
  not not_6 (not_6_out, Instr[26]);
  Demultiplexer #(.select(5), .enable("false")) demultiplexer_1 (
    .out0(demultiplexer_1_out0), .out1(demultiplexer_1_out1), .out2(demultiplexer_1_out2),
    .out3(demultiplexer_1_out3), .out4(demultiplexer_1_out4), .out5(demultiplexer_1_out5),
    .out6(demultiplexer_1_out6), .out7(demultiplexer_1_out7), .out8(demultiplexer_1_out8),
    .out9(demultiplexer_1_out9), .out10(demultiplexer_1_out10), .out11(demultiplexer_1_out11),
    .out12(demultiplexer_1_out12), .out13(demultiplexer_1_out13), .out14(demultiplexer_1_out14),
    .out15(demultiplexer_1_out15), .out16(demultiplexer_1_out16), .out17(demultiplexer_1_out17),
    .out18(demultiplexer_1_out18), .out19(demultiplexer_1_out19), .out20(demultiplexer_1_out20),
    .out21(demultiplexer_1_out21), .out22(demultiplexer_1_out22), .out23(demultiplexer_1_out23),
    .out24(demultiplexer_1_out24), .out25(demultiplexer_1_out25), .out26(demultiplexer_1_out26),
    .out27(demultiplexer_1_out27), .out28(demultiplexer_1_out28), .out29(demultiplexer_1_out29),
    .out30(demultiplexer_1_out30), .out31(demultiplexer_1_out31), .in(RegWrite), .sel(RegAddr));
  not not_7 (not_7_out, Instr[5]);
  not not_8 (not_8_out, Instr[3]);
  not not_9 (not_9_out, Instr[4]);
  not not_10 (not_10_out, Instr[2]);
  not not_11 (not_11_out, Instr[1]);
  Subtractor #(.width(32)) subtractor_1 (.a(pc), .b(32'h3000), .out(subtractor_1_out));  // open: bin, bout
  not not_12 (not_12_out, Instr[0]);
  Shifter #(.width(32), .shift("lr")) shifter_2 (.in(subtractor_1_out), .\dist (5'b00010), .out(shifter_2_out));
  BitSelector #(.width(32), .group(16)) bitselector_1 (.in(shifter_2_out), .out(bitselector_1_out), .sel(1'b0));
  and and_2 (and_2_out, not_1_out, not_2_out, not_3_out, not_4_out, not_5_out, not_6_out);
  and and_3 (and_3_out, Instr[5], not_9_out, not_8_out, not_10_out, not_11_out, not_12_out);
  and and_4 (and_4_out, not_1_out, not_2_out, not_3_out, not_4_out, not_5_out, not_6_out);
  and and_5 (and_5_out, Instr[5], not_9_out, not_8_out, not_10_out, Instr[1], not_12_out);
  and and_6 (and_6_out, not_1_out, not_2_out, Instr[29], Instr[28], not_5_out, Instr[26]);
  and and_7 (and_7_out, Instr[31], not_2_out, not_3_out, not_4_out, Instr[27], Instr[26]);
  and and_8 (and_8_out, Instr[31], not_2_out, Instr[29], not_4_out, Instr[27], Instr[26]);
  and and_9 (and_9_out, not_1_out, not_2_out, not_3_out, Instr[28], not_5_out, not_6_out);
  and and_10 (and_10_out, not_1_out, not_2_out, Instr[29], Instr[28], Instr[27], Instr[26]);
  and and_11 (and_11_out, not_1_out, not_2_out, not_3_out, not_4_out, not_5_out, not_6_out);
  and and_12 (and_12_out, not_7_out, not_9_out, not_8_out, not_10_out, not_11_out, not_12_out);
  and and_13 (and_13_out, not_1_out, not_2_out, not_3_out, not_4_out, Instr[27], Instr[26]);
  and and_14 (and_14_out, not_1_out, not_2_out, not_3_out, not_4_out, not_5_out, not_6_out);
  and and_15 (and_15_out, not_7_out, not_9_out, Instr[3], not_10_out, not_11_out, not_12_out);
  and and_16 (and_16_out, not_1_out, not_2_out, Instr[29], not_4_out, not_5_out, not_6_out);
  and and_17 (and_17_out, and_2_out, and_3_out);
  and and_18 (and_18_out, and_4_out, and_5_out);
  and and_19 (and_19_out, and_11_out, and_12_out);
  and and_20 (and_20_out, and_14_out, and_15_out);
  Register #(.width(32)) _0 (.D({32{1'b0}}), .en(demultiplexer_1_out0), .Q(_0_q), .clk(clock_1_out), .clr(in_1));
  Register #(.width(32)) _8 (.D(RegData), .en(demultiplexer_1_out8), .Q(_8_q), .clk(clock_1_out), .clr(in_1));
  Register #(.width(32)) _16 (.D(RegData), .en(demultiplexer_1_out16), .Q(_16_q), .clk(clock_1_out), .clr(in_1));
  Register #(.width(32)) _24 (.D(RegData), .en(demultiplexer_1_out24), .Q(_24_q), .clk(clock_1_out), .clr(in_1));
  or or_1 (or_1_out, and_17_out, and_18_out);
  ROM #(.addrWidth(16), .dataWidth(32)) rom_1 (.addr(bitselector_1_out), .data(Instr));  // open: sel
  Register #(.width(32)) _1 (.D(RegData), .en(demultiplexer_1_out1), .Q(_1_q), .clk(clock_1_out), .clr(in_1));
  Register #(.width(32)) _9 (.D(RegData), .en(demultiplexer_1_out9), .Q(_9_q), .clk(clock_1_out), .clr(in_1));
  Register #(.width(32)) _17 (.D(RegData), .en(demultiplexer_1_out17), .Q(_17_q), .clk(clock_1_out), .clr(in_1));
  Register #(.width(32)) _25 (.D(RegData), .en(demultiplexer_1_out25), .Q(_25_q), .clk(clock_1_out), .clr(in_1));
  or or_2 (RegWrite, and_17_out, and_18_out, and_6_out, and_16_out, and_7_out, and_10_out, and_13_out);
  Register #(.width(32)) _2 (.D(RegData), .en(demultiplexer_1_out2), .Q(_2_q), .clk(clock_1_out), .clr(in_1));
  Register #(.width(32)) _10 (.D(RegData), .en(demultiplexer_1_out10), .Q(_10_q), .clk(clock_1_out), .clr(in_1));
  Register #(.width(32)) _18 (.D(RegData), .en(demultiplexer_1_out18), .Q(_18_q), .clk(clock_1_out), .clr(in_1));
  Register #(.width(32)) _26 (.D(RegData), .en(demultiplexer_1_out26), .Q(_26_q), .clk(clock_1_out), .clr(in_1));
  assign bit_extender_2_out = {{16{1'b0}}, Instr[15:0]};  // Bit_Extender bit_extender_2
  assign bit_extender_3_out = {{16{Instr[15]}}, Instr[15:0]};  // Bit_Extender bit_extender_3
  buf or_3 (or_3_out, and_7_out);  // OR_Gate
  Register #(.width(32)) _3 (.D(RegData), .en(demultiplexer_1_out3), .Q(_3_q), .clk(clock_1_out), .clr(in_1));
  Register #(.width(32)) _11 (.D(RegData), .en(demultiplexer_1_out11), .Q(_11_q), .clk(clock_1_out), .clr(in_1));
  Register #(.width(32)) _19 (.D(RegData), .en(demultiplexer_1_out19), .Q(_19_q), .clk(clock_1_out), .clr(in_1));
  Register #(.width(32)) _27 (.D(RegData), .en(demultiplexer_1_out27), .Q(_27_q), .clk(clock_1_out), .clr(in_1));
  buf or_4 (MemWrite, and_8_out);  // OR_Gate
  Register #(.width(32)) _4 (.D(RegData), .en(demultiplexer_1_out4), .Q(_4_q), .clk(clock_1_out), .clr(in_1));
  Register #(.width(32)) _12 (.D(RegData), .en(demultiplexer_1_out12), .Q(_12_q), .clk(clock_1_out), .clr(in_1));
  Register #(.width(32)) _20 (.D(RegData), .en(demultiplexer_1_out20), .Q(_20_q), .clk(clock_1_out), .clr(in_1));
  Register #(.width(32)) _28 (.D(RegData), .en(demultiplexer_1_out28), .Q(_28_q), .clk(clock_1_out), .clr(in_1));
  Multiplexer #(.width(32), .enable("false")) multiplexer_6 (
    .in0(bit_extender_2_out), .in1(bit_extender_3_out), .out(multiplexer_6_out), .sel(or_11_out));
  Register #(.width(32)) _5 (.D(RegData), .en(demultiplexer_1_out5), .Q(_5_q), .clk(clock_1_out), .clr(in_1));
  Register #(.width(32)) _13 (.D(RegData), .en(demultiplexer_1_out13), .Q(_13_q), .clk(clock_1_out), .clr(in_1));
  Register #(.width(32)) _21 (.D(RegData), .en(demultiplexer_1_out21), .Q(_21_q), .clk(clock_1_out), .clr(in_1));
  Register #(.width(32)) _29 (.D(RegData), .en(demultiplexer_1_out29), .Q(_29_q), .clk(clock_1_out), .clr(in_1));
  buf or_5 (or_5_out, and_7_out);  // OR_Gate
  Register #(.width(32)) _6 (.D(RegData), .en(demultiplexer_1_out6), .Q(_6_q), .clk(clock_1_out), .clr(in_1));
  Register #(.width(32)) _14 (.D(RegData), .en(demultiplexer_1_out14), .Q(_14_q), .clk(clock_1_out), .clr(in_1));
  Register #(.width(32)) _22 (.D(RegData), .en(demultiplexer_1_out22), .Q(_22_q), .clk(clock_1_out), .clr(in_1));
  Register #(.width(32)) _30 (.D(RegData), .en(demultiplexer_1_out30), .Q(_30_q), .clk(clock_1_out), .clr(in_1));
  or or_6 (or_6_out, and_6_out, and_7_out, and_8_out, and_10_out, and_16_out);
  Register #(.width(32)) _7 (.D(RegData), .en(demultiplexer_1_out7), .Q(_7_q), .clk(clock_1_out), .clr(in_1));
  Register #(.width(32)) _15 (.D(RegData), .en(demultiplexer_1_out15), .Q(_15_q), .clk(clock_1_out), .clr(in_1));
  Register #(.width(32)) _23 (.D(RegData), .en(demultiplexer_1_out23), .Q(_23_q), .clk(clock_1_out), .clr(in_1));
  Register #(.width(32)) _31 (.D(RegData), .en(demultiplexer_1_out31), .Q(_31_q), .clk(clock_1_out), .clr(in_1));
  buf or_7 (or_7_out, and_9_out);  // OR_Gate
  buf or_8 (or_8_out, and_19_out);  // OR_Gate
  buf or_9 (and_1_out[1], and_13_out);  // OR_Gate
  buf or_10 (and_1_out[2], and_20_out);  // OR_Gate
  or or_11 (or_11_out, and_7_out, and_8_out, and_9_out, and_16_out);
  Multiplexer #(.select(5), .width(32), .enable("false")) multiplexer_7 (
    .in0(_0_q), .in1(_1_q), .in2(_2_q), .in3(_3_q), .in4(_4_q), .in5(_5_q), .in6(_6_q), .in7(_7_q),
    .in8(_8_q), .in9(_9_q), .in10(_10_q), .in11(_11_q), .in12(_12_q), .in13(_13_q), .in14(_14_q),
    .in15(_15_q), .in16(_16_q), .in17(_17_q), .in18(_18_q), .in19(_19_q), .in20(_20_q), .in21(_21_q),
    .in22(_22_q), .in23(_23_q), .in24(_24_q), .in25(_25_q), .in26(_26_q), .in27(_27_q), .in28(_28_q),
    .in29(_29_q), .in30(_30_q), .in31(_31_q), .out(multiplexer_7_out), .sel(Instr[25:21]));
  Multiplexer #(.select(5), .width(32), .enable("false")) multiplexer_8 (
    .in0(_0_q), .in1(_1_q), .in2(_2_q), .in3(_3_q), .in4(_4_q), .in5(_5_q), .in6(_6_q), .in7(_7_q),
    .in8(_8_q), .in9(_9_q), .in10(_10_q), .in11(_11_q), .in12(_12_q), .in13(_13_q), .in14(_14_q),
    .in15(_15_q), .in16(_16_q), .in17(_17_q), .in18(_18_q), .in19(_19_q), .in20(_20_q), .in21(_21_q),
    .in22(_22_q), .in23(_23_q), .in24(_24_q), .in25(_25_q), .in26(_26_q), .in27(_27_q), .in28(_28_q),
    .in29(_29_q), .in30(_30_q), .in31(_31_q), .out(MemData), .sel(Instr[20:16]));
  assign and_21_out = multiplexer_7_out & 32'hfffffffc;  // AND_Gate and_21, 32 bits wide
  Multiplexer #(.width(32), .enable("false")) multiplexer_9 (
    .in0(MemData), .in1(multiplexer_6_out), .out(multiplexer_9_out), .sel(or_6_out));
  Priority_Encoder #(.select(4)) priority_encoder_1 (
    .in0(and_19_out), .in1(and_17_out), .in2(and_18_out), .in3(and_6_out), .in4(and_10_out), .in5(and_7_out),
    .in6(and_8_out), .in7(and_9_out), .in8(and_16_out), .out(priority_encoder_1_out),
    .gs(priority_encoder_1_gs));  // open: in9, in10, in11, in12, in13, in14, in15, en_out, en_in
  Adder #(.width(32)) adder_3 (.a(multiplexer_7_out), .b(multiplexer_9_out), .out(adder_3_out));  // open: cin, cout
  Subtractor #(.width(32)) subtractor_2 (
    .a(multiplexer_7_out), .b(multiplexer_9_out), .out(subtractor_2_out));  // open: bin, bout
  assign or_12_out = multiplexer_7_out | multiplexer_9_out;  // OR_Gate or_12, 32 bits wide
  Shifter #(.width(32)) shifter_3 (.in(multiplexer_9_out), .\dist (5'b10000), .out(shifter_3_out));
  RAM #(.addrWidth(16), .dataWidth(32), .bus("separate")) ram_1 (
    .addr(MemAddr[17:2]), .din(MemData), .data(ram_1_data), .str(MemWrite), .clk(clock_1_out), .clr(in_1));  // open: sel, ld
  Multiplexer #(.select(4), .width(32), .enable("false")) multiplexer_10 (
    .in1(adder_3_out), .in2(subtractor_2_out), .in3(or_12_out), .in4(shifter_3_out), .in5(adder_3_out),
    .in6(adder_3_out), .in7(subtractor_2_out), .in8(adder_3_out), .out(MemAddr), .sel(priority_encoder_1_out));  // open: in0, in9, in10, in11, in12, in13, in14, in15
  Comparator #(.width(32), .mode("unsigned")) comparator_1 (
    .a(MemAddr), .b({32{1'b0}}), .eq(comparator_1_eq));  // open: gt, lt
  Clock clock_1 (.out(clock_1_out));

  // Notes on the sheet:
  //   add
  //   sub
  //   ori
  //   lw
  //   sw
  //   beq
  //   lui
  //   nop
  //   jal
  //   jr
  //   RegDst
  //   contents of rom_1 (hex, n*v repeats v):
  //   341c0000 341d0000 34013456 210820 8c010004 ac010004 3c027878 411822 3c051234 34040005 0 ac85ffff
  //   8c83ffff 10650001 1000000d 34670404 10e3000b 0 3c087777 3508ffff 80022 34001100 e65020 34080000
  //   34090001 340a0001 10a4020 1109fffe 1000ffff
  //   RegWrite
  //   func
  //   rd
  //   rt
  //   rs
  //   opcode
  //   MemToReg
  //   MemWrite
  //   add
  //   sub
  //   ori
  //   lw
  //   sw
  //   beq
  //   lui
  //   nop
  //   jal
  //   jr
  //   MemRead
  //   ALUSrcI
  //   beq
  //   nop
  //   jal
  //   add
  //   sub
  //   ori
  //   lw
  //   sw
  //   beq
  //   lui
  //   nop
  //   jal
  //   jr
  //   jr
  //   ExtOp
  //   add
  //   sub
  //   ori
  //   lw
  //   sw
  //   beq
  //   lui
  //   nop
  //   jal
  //   jr
endmodule
